# Fritzing sketch telemetria_AVES (saved by Fritzing 0.9.3b)
breadboards: 2

parts:
  Componente1 = Arduino Nano (Rev3.0)
  Componente2 = Arduino Nano (Rev3.0)
  U1 = SUP500F [package=sup500f]
  GY2 = MPU-6050 Board GY-521 [form="♀ (female)" package=THT]
  BAT1 = BC9VPC [package=bc9vpc]
  LED1 = LED - 3mm [color="Red (633nm)" package="3 mm [THT]"]
  LED2 = LED - 3mm [color="Red (633nm)" package="3 mm [THT]"]
  LED3 = LED - 3mm [color="Green (565nm)" package="3 mm [THT]"]
  LED4 = LED - 3mm [color="Green (565nm)" package="3 mm [THT]"]
  R1 = Resistor [tolerance=±5% resistance=1k package=THT]
  R2 = Resistor [tolerance=±5% resistance=1k package=THT]
  R3 = Resistor [tolerance=±5% resistance=1k package=THT]
  R4 = Resistor [tolerance=±5% resistance=1k package=THT]
  S1 = Pushbutton [package="[THT]"]
  Componente3 = MicroSD Card Module
  Componente4 = MicroSD Card Module
  S2 = Toggle Switch [package=THT]
  J1 = female pin header, 4 pins [form="♀ (female)"]
  Componente6 = Tiny RTC - DS1307 Breakout Board
  J2 = female pin header, 6 pins [form="♀ (female)"]
  R5 = Resistor [tolerance=±5% resistance=1k package=THT]

nets:
  GND: Componente1.GND, Componente2.GND, U1.GND, GY2.pin2, BAT1.V-, LED1.cathode, LED2.cathode, LED3.cathode, LED4.cathode, Componente3.GND, Componente4.GND, J1.pin2, Componente6.GND, J2.pin6, R5.Pin_1
  N1: Componente1.D2, U1.TX-O
  N2: Componente1.D3, U1.RX-I
  N3: Componente1.D5, Componente2.D8, S1.Pin_1, S1.Pin_2, R5.Pin_0
  N4: Componente1.D6, R4.Pin_0
  N5: Componente1.D7, R3.Pin_0
  N6: Componente1.D10, Componente3.CS
  N7: Componente1.D11/MOSI, Componente3.MOSI
  N8: Componente1.D12/MISO, Componente3.MISO
  VIN: Componente1.VIN, Componente2.VIN, S2.L2
  VCC: Componente1.5V, U1.VCC, Componente3.VCC
  N9: Componente1.D13/SCK, Componente3.SCK
  N10: Componente2.D2, Componente6.SDA
  N11: Componente2.D3, Componente6.SCL
  N12: Componente2.D6, R2.Pin_0
  N13: Componente2.D7, R1.Pin_0
  N14: Componente2.D10, Componente4.CS
  N15: Componente2.D11/MOSI, Componente4.MOSI
  N16: Componente2.D12/MISO, Componente4.MISO
  VCC_2: Componente2.5V, GY2.pin1, S1.Pin_3, S1.Pin_4, Componente4.VCC, J1.pin1, Componente6.VCC, J2.pin1
  N17: Componente2.A5, GY2.pin3, J1.pin4, J2.pin3
  N18: Componente2.A4, GY2.pin4, J1.pin3, J2.pin2
  N19: Componente2.D13/SCK, Componente4.SCK
  N20: BAT1.V+, S2.COM
  N21: LED1.anode, R1.Pin_1
  N22: LED2.anode, R3.Pin_1
  N23: LED3.anode, R4.Pin_1
  N24: LED4.anode, R2.Pin_1

custom parts:
  MPU-6050 Board GY-521: Acelerometro y Giroscopio MPU-6050 Board GY-521
  Tiny RTC - DS1307 Breakout Board: The Tiny RTC is a breakout board for the Dallas Semiconductor/Maxim Integrated DS1307 real-time clock. The DS1307 counts seconds, minutes, hours, date of the month, month, day of the week, and year (with compensation for leap-years). The breakout board also has space for a DS18B20 digital thermometer.
